// Digital circuit lcd.dig as structural Verilog
module lcd (
  input  OE,
  input  [7:0] D,
  input  CP,
  input  CLK,
  input  EN
);

  wire _7408_1_pin3, _7408_1_pin9, _7408_1_pin10, _7408_1_pin12, _7408_1_pin13, _7414_1_pin2, _7414_1_pin3,
       _7414_1_pin4, _7414_1_pin6, _7414_1_pin9, _7414_1_pin11, _7414_1_pin13, bussplitter_1_d0,
       bussplitter_1_d1, bussplitter_1_d2, bussplitter_1_d3, bussplitter_1_d7, driver_1_out, driver_2_out,
       driver_4_out, not_1_out, undriven, undriven_2, undriven_3, undriven_4, undriven_5, undriven_6;
  wire [2:0] bussplitter_1_d4;
  wire [3:0] bussplitter_2_d0;
  wire [7:0] bussplitter_2_d, driver_3_out;

  assign driver_1_out = EN ? CP : 1'bz;  // Driver driver_1
  assign driver_2_out = EN ? OE : 1'bz;  // Driver driver_2
  assign driver_3_out = EN ? D : 8'bz;  // Driver driver_3
  assign driver_4_out = EN ? CLK : 1'bz;  // Driver driver_4
  BusSplitter #(.Bits(8)) bussplitter_1 (
    .D(driver_3_out), .OE(driver_2_out), .D0(bussplitter_1_d0), .D1(bussplitter_1_d1), .D2(bussplitter_1_d2),
    .D3(bussplitter_1_d3), .D4(bussplitter_1_d4[0]), .D5(bussplitter_1_d4[1]), .D6(bussplitter_1_d4[2]),
    .D7(bussplitter_1_d7));
  BusSplitter #(.Bits(8)) bussplitter_2 (
    .D(bussplitter_2_d), .OE(_7414_1_pin6), .D0(bussplitter_2_d0[0]), .D1(bussplitter_2_d0[1]),
    .D2(bussplitter_2_d0[2]), .D3(bussplitter_2_d0[3]), .D4(bussplitter_1_d0), .D5(bussplitter_1_d1),
    .D6(bussplitter_1_d2), .D7(bussplitter_1_d3));
  // NotConnected on bussplitter_2_d0
  // NotConnected on bussplitter_1_d4
  _7414 _7414_1 (
    .pin1(driver_1_out), .pin2(_7414_1_pin2), .pin3(_7414_1_pin3), .pin4(_7414_1_pin4), .pin5(driver_2_out),
    .pin6(_7414_1_pin6), .pin7(1'b0), .pin9(_7414_1_pin9), .pin11(_7414_1_pin11), .pin13(_7414_1_pin13),
    .pin14(1'b1));  // open: pin8, pin10, pin12
  _7408 _7408_1 (
    .pin1(driver_2_out), .pin2(bussplitter_1_d7), .pin3(_7408_1_pin3), .pin4(_7414_1_pin2),
    .pin5(driver_2_out), .pin6(_7414_1_pin3), .pin7(1'b0), .pin9(_7408_1_pin9), .pin10(_7408_1_pin10),
    .pin12(_7408_1_pin12), .pin13(_7408_1_pin13), .pin14(1'b1));  // open: pin8, pin11
  // NotConnected on _7414_1_pin13
  // NotConnected on _7414_1_pin11
  // NotConnected on _7414_1_pin9
  // NotConnected on _7408_1_pin13
  // NotConnected on _7408_1_pin12
  // NotConnected on _7408_1_pin10
  // NotConnected on _7408_1_pin9
  HD44780U hd44780u_1 (
    .DB(bussplitter_2_d), .E(_7414_1_pin4), .RW(_7414_1_pin6), .RS(_7408_1_pin3), .clk(driver_4_out));  // open: CLK_2
  // Probe on undriven
  // Probe on undriven_2
  // Probe on undriven_3
  // Probe on undriven_4
  // Probe on undriven_5
  not not_1 (not_1_out, undriven_3);
  // Probe on undriven_6
  Break #(.Cycles(1000000000)) break_1 (.brk(undriven_6));
  Break #(.Cycles(1000000000)) break_2 (.brk(not_1_out));
endmodule

/* Test case:
OE_ CP D_out
1   X  Z
*/
