// Digital circuit lutcomp.dig as structural Verilog
module lutcomp (
  input  RESET,
  input  clk,
  output HALT
);

  wire and_1_out, and_3_out, CLK_t, CLK_t_t, counter_1_ovf, decoder_1_out_0, decoder_1_out_1,
       decoder_1_out_2, decoder_1_out_3, decoder_1_out_4, decoder_1_out_5, decoder_1_out_6, decoder_1_out_7,
       io_1_io0_cp, io_1_io0_oe, io_1_io2_oe, not_1_out, not_3_out, not_4_out, not_5_out,
       ps2_decoder_1_ps2_ready, ps2_encoder_1_ack, PS2_Keyboard_av, switch_1_b, TTYIN_av, uc_1_p3, uc_1_p5,
       uc_1_p7, uc_1_p8, uc_1_p9, uc_1_p10, uc_1_p11, uc_1_p12, uc_1_p13, uc_1_p14, uc_1_p15, uc_1_p16,
       uc_1_p17, uc_1_p19, uc_1_p20, uc_1_p21, uc_1_p22, undriven, undriven_2, undriven_3, undriven_4,
       undriven_9, undriven_10, undriven_11, undriven_12, undriven_13, undriven_14, undriven_15, undriven_16,
       undriven_17, undriven_18, undriven_20, undriven_21, undriven_22, undriven_23;
  wire [2:0] uc_1_p6, undriven_19;
  wire [3:0] undriven_7;
  wire [6:0] undriven_5;
  wire [7:0] counter_4_out, rom_1_d, uc_1_p4, undriven_6;
  wire [9:0] counter_1_out;
  wire [15:0] counter_3_out, TTYIN_d;
  wire [15:7] PS2_Keyboard_d;
  wire [23:0] pc_1_pc, undriven_8;
  wire [63:0] counter_2_out;

  Keyboard PS2_Keyboard (.C(counter_1_ovf), .en(1'b1), .D({PS2_Keyboard_d, counter_1_out[9:3]}), .av(PS2_Keyboard_av));
  Counter #(.Bits(3)) counter_1 (
    .en(PS2_Keyboard_av), .C(ps2_encoder_1_ack), .clr(1'b0), .out(counter_1_out[2:0]), .ovf(counter_1_ovf));
  ROM #(.AddrBits(10), .Bits(8)) rom_1 (.A(counter_1_out), .sel(1'b1), .D(rom_1_d));
  and and_1 (and_1_out, CLK_t, PS2_Keyboard_av);
  and and_2 (CLK_t, clk, HALT);
  Stop stop_1 (.stop(~HALT));
  not not_1 (not_1_out, HALT);
  ps2_encoder ps2_encoder_1 (
    .CLK(and_1_out), .DATA(rom_1_d), .PS2_CLK(undriven_23), .PS2_DATA(undriven_22), .ACK(ps2_encoder_1_ack));
  Break #(.Cycles(1000000000)) break_1 (.brk(not_1_out));
  not not_2 (CLK_t_t, CLK_t);
  // Probe TickCount on counter_2_out
  Counter #(.Bits(64)) counter_2 (.en(1'b1), .C(CLK_t), .clr(1'b0), .out(counter_2_out));  // open: ovf
  ps2_decoder ps2_decoder_1 (
    .PS2_CP(io_1_io2_oe), .DATA(uc_1_p4), .PS2_OE(io_1_io2_oe), .PS2_CLK(undriven_23),
    .PS2_DATA(undriven_22), .PS2_READY(ps2_decoder_1_ps2_ready));
  // uc uc_1: pin names not known; wires that end beside it: CLK_t_t, RESET, uc_1_p3, uc_1_p4, uc_1_p5, uc_1_p6, uc_1_p7, uc_1_p8, uc_1_p9, uc_1_p10, uc_1_p11, uc_1_p12, uc_1_p13, uc_1_p14, uc_1_p15, uc_1_p16, uc_1_p17, HALT, uc_1_p19, uc_1_p20, uc_1_p21, uc_1_p22
  // Probe on ps2_decoder_1_ps2_ready
  not not_3 (not_3_out, uc_1_p5);
  // Probe on undriven_12
  // Probe on undriven_13
  // Probe on undriven_14
  // Probe on undriven_15
  // Probe on undriven_16
  // Probe on undriven_21
  and and_3 (and_3_out, uc_1_p7, ~uc_1_p22);  // And
  Switch switch_1 (.A(uc_1_p7), .B(switch_1_b));
  pc pc_1 (.PC_INC(uc_1_p7), .RESET(RESET), .PC_SPE(uc_1_p22), .OE(not_3_out), .ADDR(undriven_8), .PC(pc_1_pc));
  not not_4 (not_4_out, uc_1_p21);
  Break #(.Cycles(1000000000)) break_2 (.brk(undriven_17));
  not not_5 (not_5_out, undriven_18);
  Counter #(.Bits(16)) counter_3 (.en(1'b1), .C(uc_1_p7), .clr(1'b0), .out(counter_3_out));  // open: ovf
  Break #(.Cycles(10000000)) break_3 (.brk(switch_1_b));
  PullDown pulldown_1 (.out(switch_1_b));
  Break #(.Cycles(1000000000)) break_4 (.brk(not_4_out));
  // Probe $uPC on {undriven_7, undriven_6, undriven_5}
  // Probe on undriven_5
  // Probe $IR0 on undriven_6
  // Probe $FLAGS on undriven_7
  Break #(.Cycles(1000000000)) break_5 (.brk(not_5_out));
  io io_1 (
    .DATA(uc_1_p4), .IO_SEL(undriven_19), .IO_OE(undriven_20), .IO_CP(undriven_17),
    .IO_AVAIL_OE(undriven_18), .IO0_AVAIL(TTYIN_av), .IO1_AVAIL(1'b0), .IO2_AVAIL(ps2_decoder_1_ps2_ready),
    .IO3_AVAIL(1'b0), .IO4_AVAIL(1'b0), .IO5_AVAIL(1'b0), .IO6_AVAIL(1'b0), .IO7_AVAIL(1'b0),
    .IO_AVAIL(uc_1_p3), .IO0_CP(io_1_io0_cp), .IO0_OE(io_1_io0_oe), .IO2_OE(io_1_io2_oe));  // open: IO1_CP, IO1_OE, IO2_CP, IO3_CP, IO3_OE, IO4_CP, IO4_OE, IO5_CP, IO5_OE, IO6_CP, IO6_OE, IO7_CP, IO7_OE
  Counter #(.Bits(8)) counter_4 (.en(1'b1), .C(and_3_out), .clr(1'b0), .out(counter_4_out));  // open: ovf
  // Probe PC on pc_1_pc
  RAMDualPort #(.AddrBits(16), .Bits(24)) PC_LOG (
    .A(counter_3_out), .Din(pc_1_pc), .str(1'b1), .C(uc_1_p7), .ld(1'b0));  // open: D
  RAMDualPort #(.AddrBits(8), .Bits(24)) JMP_LOG (
    .A(counter_4_out), .Din(pc_1_pc), .str(1'b1), .C(and_3_out), .ld(1'b0));  // open: D
  memory memory_1 (
    .MEM_WE(uc_1_p10), .ADDR_OE(uc_1_p5), .A0_CP(uc_1_p15), .A1_CP(uc_1_p16), .A2_CP(uc_1_p17),
    .MEM_OE(uc_1_p20), .DATA(uc_1_p4), .ADDR(undriven_8), .A0_OE(undriven_11), .A1_OE(undriven_10),
    .A2_OE(undriven_9));
  // Probe ADDR on undriven_8
  // Probe DATA on uc_1_p4
  Keyboard TTYIN (.C(io_1_io0_oe), .en(1'b1), .D(TTYIN_d), .av(TTYIN_av));
  Break break_6 (.brk(io_1_io0_oe));
  assign uc_1_p4 = ~io_1_io0_oe ? TTYIN_d[7:0] : 8'bz;  // DriverInvSel driverinvsel_1
  Decoder #(.Selector_Bits(3)) decoder_1 (
    .sel(uc_1_p6), .out_0(decoder_1_out_0), .out_1(decoder_1_out_1), .out_2(decoder_1_out_2),
    .out_3(decoder_1_out_3), .out_4(decoder_1_out_4), .out_5(decoder_1_out_5), .out_6(decoder_1_out_6),
    .out_7(decoder_1_out_7));
  alu alu_1 (.ALU_OP(uc_1_p6), .ALU_OE(uc_1_p19), .ALU_CP(uc_1_p9), .IN1_CP(uc_1_p8), .DATA(uc_1_p4));
  \reg  W (.OE(undriven), .CP(uc_1_p11), .IO(uc_1_p4));
  \reg  X (.OE(undriven_2), .CP(uc_1_p12), .IO(uc_1_p4));
  \reg  Y (.OE(undriven_3), .CP(uc_1_p13), .IO(uc_1_p4));
  \reg  Z (.OE(undriven_4), .CP(uc_1_p14), .IO(uc_1_p4));
  Terminal TTYOUT (.D(uc_1_p4), .C(io_1_io0_cp), .en(1'b1));
  // Probe AddLo on decoder_1_out_0
  // Probe AddHiNC on decoder_1_out_2
  // Probe Or on decoder_1_out_4
  // Probe And on decoder_1_out_6
  // Probe MulHi on decoder_1_out_1
  // Probe AddHiC on decoder_1_out_3
  // Probe Div on decoder_1_out_5
  // Probe Special on decoder_1_out_7

  // Notes on the sheet:
  //   RESET: default 1
  //   clk: Hz: 100000
  //   PS2 Keyboard
  //   rom_1 loads ascii_to_ps2.hex
  //   4A
  //   4B
  //   4Y
  //   6A
  //   6Y
  //   3A
  //   3Y
  //   TTY
endmodule

/* Test case:
RESET_ HALT_
0      1
*/
